# Fritzing sketch SmartFarm (saved by Fritzing 0.9.3b)
breadboards: 2

parts:
  Componente1 = Arduino Uno (Rev3) - ICSP
  LED2 = LEDs [package=led10mm]
  R5 = Resistor [tolerance=±5% resistance=220 package=THT]
  R1 = Photocell (LDR) [package=THT]
  R7 = Resistor [tolerance=±5% resistance=220 package=THT]
  Q5 = NPN-Transistor [package="TO92 [THT]"]
  R8 = Resistor [tolerance=±5% resistance=220 package=THT]
  R9 = Photocell (LDR) [package=THT]
  R10 = Resistor [tolerance=±5% resistance=220 package=THT]
  R11 = Resistor [tolerance=±5% resistance=220 package=THT]
  R12 = Photocell (LDR) [package=THT]
  R13 = Resistor [tolerance=±5% resistance=220 package=THT]
  R14 = Resistor [tolerance=±5% resistance=220 package=THT]
  R15 = Photocell (LDR) [package=THT]
  R16 = Resistor [tolerance=±5% resistance=220 package=THT]
  LED5 = LEDs [package=led10mm]
  Q6 = NPN-Transistor [package="TO92 [THT]"]
  LED6 = LEDs [package=led10mm]
  Q7 = NPN-Transistor [package="TO92 [THT]"]
  LED7 = LEDs [package=led10mm]
  Q8 = NPN-Transistor [package="TO92 [THT]"]
  Componente2 = Photon
  S1 = Round Pushbutton  # not connected

nets:
  N1: Componente1.A2, R10.Pin_1
  N2: Componente1.A3, R7.Pin_1
  N3: Componente1.A4/SDA, R13.Pin_1
  N4: Componente1.A5/SCL, R16.Pin_1
  N5: Componente1.D9_PWM, R14.Pin_0
  N6: Componente1.D10_PWM/SS, R5.Pin_0
  GND: Componente1.GND, Q5.C, Q6.C, Q7.C, Q8.C, Componente2.GND
  N7: Componente1.D2, Componente2.TX
  N8: Componente1.D3_PWM, Componente2.RX
  N9: Componente1.D5_PWM, R8.Pin_0
  N10: Componente1.D6_PWM, R11.Pin_0
  N11: Componente1.5V, R1.pin_0
  N12: LED2.C, Q5.B
  N13: LED2.A, LED5.A, LED6.A, LED7.A
  N14: R5.Pin_1, Q5.E
  N15: R1.pin_1, R7.Pin_0
  N16: R8.Pin_1, Q6.E
  N17: R9.pin_1, R10.Pin_0
  N18: R11.Pin_1, Q7.E
  N19: R12.pin_1, R13.Pin_0
  N20: R14.Pin_1, Q8.E
  N21: R15.pin_1, R16.Pin_0
  N22: LED5.C, Q6.B
  N23: LED6.C, Q7.B
  N24: LED7.C, Q8.B

notes:
  Batería 12V
